// Logisim project 16-bit common bus.circ as structural Verilog: 1 circuit, main circuit main
module main (
  input  [2:0] in_1,
  input  [15:0] in_2,
  input  [15:0] in_3,
  input  [15:0] in_4,
  input  [11:0] in_5,
  input  [15:0] in_6,
  input  [11:0] in_7,
  input  [15:0] in_8,
  output out_9,
  output out_10,
  output out_11,
  output out_12,
  output out_13,
  output out_14,
  output out_15,
  output out_16,
  output out_17,
  output out_18,
  output out_19,
  output out_20,
  output out_21,
  output out_22,
  output out_23,
  output out_24
);

  Multiplexer #(.select(3), .enable("false")) multiplexer_1 (
    .in1(in_7[0]), .in2(in_5[0]), .in3(in_6[0]), .in4(in_3[0]), .in5(in_2[0]), .in6(in_4[0]), .in7(in_8[0]),
    .out(out_24), .sel(in_1));  // open: in0
  Multiplexer #(.select(3), .enable("false")) multiplexer_2 (
    .in1(in_7[1]), .in2(in_5[1]), .in3(in_6[1]), .in4(in_3[1]), .in5(in_2[1]), .in6(in_4[1]), .in7(in_8[1]),
    .out(out_23), .sel(in_1));  // open: in0
  Multiplexer #(.select(3), .enable("false")) multiplexer_3 (
    .in1(in_7[2]), .in2(in_5[2]), .in3(in_6[2]), .in4(in_3[2]), .in5(in_2[2]), .in6(in_4[2]), .in7(in_8[2]),
    .out(out_22), .sel(in_1));  // open: in0
  Multiplexer #(.select(3), .enable("false")) multiplexer_4 (
    .in1(in_7[3]), .in2(in_5[3]), .in3(in_6[3]), .in4(in_3[3]), .in5(in_2[3]), .in6(in_4[3]), .in7(in_8[3]),
    .out(out_21), .sel(in_1));  // open: in0
  Multiplexer #(.select(3)) multiplexer_5 (
    .in1(in_7[4]), .in2(in_5[4]), .in3(in_6[4]), .in4(in_3[4]), .in5(in_2[4]), .in6(in_4[4]), .in7(in_8[4]),
    .out(out_20), .sel(in_1));  // open: in0, en
  Multiplexer #(.select(3), .enable("false")) multiplexer_6 (
    .in1(in_7[5]), .in2(in_5[5]), .in3(in_6[5]), .in4(in_3[5]), .in5(in_2[5]), .in6(in_4[5]), .in7(in_8[5]),
    .out(out_19), .sel(in_1));  // open: in0
  Multiplexer #(.select(3), .enable("false")) multiplexer_7 (
    .in1(in_7[6]), .in2(in_5[6]), .in3(in_6[6]), .in4(in_3[6]), .in5(in_2[6]), .in6(in_4[6]), .in7(in_8[6]),
    .out(out_18), .sel(in_1));  // open: in0
  Multiplexer #(.select(3), .enable("false")) multiplexer_8 (
    .in1(in_7[7]), .in2(in_5[7]), .in3(in_6[7]), .in4(in_3[7]), .in5(in_2[7]), .in6(in_4[7]), .in7(in_8[7]),
    .out(out_17), .sel(in_1));  // open: in0
  Multiplexer #(.select(3), .enable("false")) multiplexer_9 (
    .in1(in_7[8]), .in2(in_5[8]), .in3(in_6[8]), .in4(in_3[8]), .in5(in_2[8]), .in6(in_4[8]), .in7(in_8[8]),
    .out(out_16), .sel(in_1));  // open: in0
  Multiplexer #(.select(3), .enable("false")) multiplexer_10 (
    .in1(in_7[9]), .in2(in_5[9]), .in3(in_6[9]), .in4(in_3[9]), .in5(in_2[9]), .in6(in_4[9]), .in7(in_8[9]),
    .out(out_15), .sel(in_1));  // open: in0
  Multiplexer #(.select(3), .enable("false")) multiplexer_11 (
    .in1(in_7[10]), .in2(in_5[10]), .in3(in_6[10]), .in4(in_3[10]), .in5(in_2[10]), .in6(in_4[10]),
    .in7(in_8[10]), .out(out_14), .sel(in_1));  // open: in0
  Multiplexer #(.select(3), .enable("false")) multiplexer_12 (
    .in1(in_7[11]), .in2(in_5[11]), .in3(in_6[11]), .in4(in_3[11]), .in5(in_2[11]), .in6(in_4[11]),
    .in7(in_8[11]), .out(out_13), .sel(in_1));  // open: in0
  Multiplexer #(.select(3), .enable("false")) multiplexer_13 (
    .in3(in_6[12]), .in4(in_3[12]), .in5(in_2[12]), .in6(in_4[12]), .in7(in_8[12]), .out(out_12), .sel(in_1));  // open: in0, in1, in2
  Multiplexer #(.select(3), .enable("false")) multiplexer_14 (
    .in3(in_6[13]), .in4(in_3[13]), .in5(in_2[13]), .in6(in_4[13]), .in7(in_8[13]), .out(out_11), .sel(in_1));  // open: in0, in1, in2
  Multiplexer #(.select(3), .enable("false")) multiplexer_15 (
    .in3(in_6[14]), .in4(in_3[14]), .in5(in_2[14]), .in6(in_4[14]), .in7(in_8[14]), .out(out_10), .sel(in_1));  // open: in0, in1, in2
  Multiplexer #(.select(3), .enable("false")) multiplexer_16 (
    .in3(in_6[15]), .in4(in_3[15]), .in5(in_2[15]), .in6(in_4[15]), .in7(in_8[15]), .out(out_9), .sel(in_1));  // open: in0, in1, in2

  // Notes on the sheet:
  //   0
  //   1
  //   2
  //   3
  //   4
  //   5
  //   6
  //   7
  //   8
  //   9
  //   10
  //   11
  //   12
  //   13
  //   14
  //   15
endmodule
