// Logisim project ALU COMP1.circ as structural Verilog: 1 circuit, main circuit main
module main (
  input  in_1,
  input  in_2,
  input  in_3,
  input  in_4,
  input  in_5,
  input  in_6,
  input  in_7,
  input  [15:0] in_8,
  input  [15:0] in_9,
  input  [7:0] in_10,
  input  in_11,
  output [15:0] out_12,
  output out_13
);

  wire adder_1_cout, and_8_out, and_9_out, and_12_out, bit_extender_3_out, bit_extender_4_out;
  wire [0:0] and_2_out;
  wire [3:0] bit_extender_1_out, bit_extender_2_out;
  wire [7:0] and_7_out;
  wire [15:0] adder_1_out, and_3_out, and_4_out, and_5_out, and_6_out, and_10_out, and_11_out,
       bit_extender_5_out, not_1_out, or_1_out, or_2_out, shifter_1_out_2, shifter_2_out;
  wire [15:15] shifter_1_out;

  assign bit_extender_1_out = {{3{1'b0}}, 1'b1};  // Bit_Extender bit_extender_1
  assign bit_extender_2_out = {{3{1'b0}}, 1'b1};  // Bit_Extender bit_extender_2
  Adder #(.width(16)) adder_1 (.a(in_9), .b(in_8), .out(adder_1_out), .cout(adder_1_cout));  // open: cin
  assign not_1_out = ~in_8;  // NOT_Gate not_1, 16 bits wide
  Shifter #(.width(16), .shift("lr")) shifter_1 (
    .in(in_8), .\dist (bit_extender_1_out), .out({shifter_1_out[15], shifter_1_out_2[14:0]}));
  Shifter #(.width(16)) shifter_2 (.in(in_8), .\dist (bit_extender_2_out), .out(shifter_2_out));
  Bit_Extender #(.in_width(16), .out_width(1)) bit_extender_3 (.in({16{in_5}}), .out(bit_extender_3_out));
  and and_1 (shifter_1_out_2[15], bit_extender_3_out, in_11);
  and and_2 (and_2_out[0], bit_extender_4_out, in_11);
  assign and_3_out = {16{in_7}} & in_9 & in_8;  // AND_Gate and_3, 16 bits wide
  assign and_4_out = {16{in_2}} & in_9;  // AND_Gate and_4, 16 bits wide
  assign and_5_out = {16{in_6}} & adder_1_out;  // AND_Gate and_5, 16 bits wide
  assign and_6_out = {16{in_3}} & not_1_out;  // AND_Gate and_6, 16 bits wide
  Bit_Extender #(.in_width(16), .out_width(1)) bit_extender_4 (.in({16{in_1}}), .out(bit_extender_4_out));
  assign and_7_out = {8{in_4}} & in_10;  // AND_Gate and_7, 8 bits wide
  and and_8 (and_8_out, in_8[15], bit_extender_4_out);
  assign or_1_out = and_3_out | and_5_out | and_4_out | and_6_out;  // OR_Gate or_1, 16 bits wide
  and and_9 (and_9_out, adder_1_cout, in_6);
  assign bit_extender_5_out = {{8{1'b0}}, and_7_out};  // Bit_Extender bit_extender_5
  assign and_10_out = {16{in_1}} & {shifter_2_out[15:1], and_2_out[0]};  // AND_Gate and_10, 16 bits wide
  assign and_11_out = {16{in_5}} & shifter_1_out_2;  // AND_Gate and_11, 16 bits wide
  assign or_2_out = bit_extender_5_out | and_10_out | and_11_out;  // OR_Gate or_2, 16 bits wide
  assign out_12 = or_1_out | or_2_out;  // OR_Gate or_3, 16 bits wide
  and and_12 (and_12_out, bit_extender_3_out, in_8[0]);
  or or_4 (out_13, and_9_out, and_8_out, and_12_out);
endmodule
