// Logisim project Computer 2.circ as structural Verilog: 1 circuit, main circuit main
module main (
  output [6:0] out_1,
  output [15:0] out_2
);

  wire and_3_out, clock_1_out, counter_1_q, main_4_add, main_4_and, main_4_clrac, main_4_comp, main_4_drtac,
       main_4_incac, main_4_incdr, main_4_incpc, main_4_ld_ac, main_4_ld_ar, main_4_ld_dr, main_4_ld_pc,
       main_4_or, main_4_read, main_4_sel_mux1, main_4_shl, main_4_shr, main_4_su8, main_4_write,
       main_4_write_2, main_4_xor, main_6_p1, not_1_out, or_2_out;
  wire [1:0] main_4_sel_s1;
  wire [2:0] rom_1_data_2, rom_1_data_3;
  wire [3:0] main_7_out_6_2;
  wire [6:0] and_1_out, and_2_out, main_5_out_6, main_6_p2, main_6_p3, or_1_out;
  wire [6:6] decoder_1_out0, decoder_1_out1;
  wire [10:0] bit_extender_1_out, main_2_out_6, main_3_out_6, multiplexer_1_out;
  wire [13:0] rom_1_data;
  wire [15:0] bit_extender_2_out, main_7_out_6, main_8_out_12, multiplexer_2_out, ram_1_data;

  _7_bit_Register_main main_1 (
    .in_4(clock_1_out), .out_6(out_1), .in_1(main_6_p2), .in_2(main_6_p1), .in_3(1'b0));  // open: in_5
  Counter #(.width(1), .max('h1), .ongoal("stay")) counter_1 (
    .Q(counter_1_q), .clk(clock_1_out));  // open: load, D, count, carry, clr
  Decoder #(.enable("false")) decoder_1 (.out0(decoder_1_out0[6]), .out1(decoder_1_out1[6]), .sel(counter_1_q));
  _11_bit_Register_main main_2 (
    .in_4(clock_1_out), .out_6(main_2_out_6), .in_1(multiplexer_1_out), .in_2(main_4_ld_ar), .in_3(1'b0));  // open: in_5
  _11_bit_Register_main main_3 (
    .in_4(clock_1_out), .out_6(main_3_out_6), .in_1(main_2_out_6), .in_2(main_4_ld_pc), .in_3(main_4_incpc));  // open: in_5
  assign and_1_out = {7{decoder_1_out0[6]}} & 7'b1000000;  // AND_Gate and_1, 7 bits wide
  assign and_2_out = {7{decoder_1_out1[6]}} & main_6_p3;  // AND_Gate and_2, 7 bits wide
  Multiplexer #(.width(11), .enable("false")) multiplexer_1 (
    .in0(main_3_out_6), .in1(bit_extender_1_out), .out(multiplexer_1_out), .sel(main_4_sel_mux1));
  buf and_3 (and_3_out, not_1_out);  // AND_Gate
  not not_1 (not_1_out, main_4_write_2);
  Control_Unit_COMP2_main main_4 (
    .ADD(main_4_add), .SU8(main_4_su8), .OR(main_4_or), .AND(main_4_and), .XOR(main_4_xor),
    .COMP(main_4_comp), .LD_AC(main_4_ld_ac), .SHL(main_4_shl), .SHR(main_4_shr), .DRTAC(main_4_drtac),
    .INCAC(main_4_incac), .CLRAC(main_4_clrac), .SEL_MUX1(main_4_sel_mux1), .LD_AR(main_4_ld_ar),
    .LD_PC(main_4_ld_pc), .INCPC(main_4_incpc), .SEL_S1(main_4_sel_s1[0]), .LD_DR(main_4_ld_dr),
    .SEL_S0(main_4_sel_s1[1]), .INCDR(main_4_incdr), .F1(rom_1_data_3), .F2(rom_1_data_2),
    .F3(rom_1_data[13:11]), .WRITE(main_4_write), .READ(main_4_read), .WRITE_2(main_4_write_2));
  Bit_Extender #(.in_width(16), .out_width(11)) bit_extender_1 (
    .in({main_7_out_6[15], main_7_out_6_2, main_7_out_6[10:0]}), .out(bit_extender_1_out));
  _7_bit_Register_main main_5 (
    .in_4(clock_1_out), .out_6(main_5_out_6), .in_1(or_1_out), .in_2(1'b1), .in_3(1'b0));  // open: in_5
  assign or_1_out = and_1_out | and_2_out;  // OR_Gate or_1, 7 bits wide
  ROM #(.addrWidth(7), .dataWidth(20)) rom_1 (
    .addr(main_5_out_6), .data({rom_1_data_3, rom_1_data_2, rom_1_data}), .sel(and_3_out));
  // MicroProgram_Sequencer_COMP2_main main_6: pin names not known; wires that end beside it: main_6_p1, main_6_p2, main_6_p3, rom_1_data[10], rom_1_data[9], rom_1_data[8], rom_1_data[7], rom_1_data[6], rom_1_data[5], rom_1_data[4], rom_1_data[3]
  or or_2 (or_2_out, main_4_read, main_4_write);
  assign bit_extender_2_out = {{5{1'b0}}, main_3_out_6};  // Bit_Extender bit_extender_2
  _16_bit_Register_main main_7 (
    .in_2(main_4_incdr), .in_4(clock_1_out), .out_6({main_7_out_6[15], main_7_out_6_2, main_7_out_6[10:0]}),
    .in_1(multiplexer_2_out), .in_3(main_4_ld_dr));  // open: in_5
  ALU_COMP2_main main_8 (
    .out_12(main_8_out_12), .in_2(out_2), .in_3({main_7_out_6[15], main_7_out_6_2, main_7_out_6[10:0]}),
    .ADD(main_4_add), .SUB(main_4_su8), .OR(main_4_or), .AND(main_4_and), .XOR(main_4_xor),
    .COMP(main_4_comp), .SHL(main_4_shl), .SHR(main_4_shr), .DRTAC(main_4_drtac));
  _16_bit_Register_main main_9 (
    .in_2(main_4_incac), .in_4(clock_1_out), .in_5(main_4_clrac), .out_6(out_2), .in_1(main_8_out_12),
    .in_3(main_4_ld_ac));
  Multiplexer #(.select(2), .width(16), .enable("false")) multiplexer_2 (
    .in0(ram_1_data), .in1(out_2), .in2(bit_extender_2_out), .out(multiplexer_2_out), .sel(main_4_sel_s1));  // open: in3
  RAM #(.addrWidth(11), .dataWidth(16), .bus("separate")) ram_1 (
    .addr(main_2_out_6), .din({main_7_out_6[15], main_7_out_6_2, main_7_out_6[10:0]}), .data(ram_1_data),
    .str(main_4_write), .sel(or_2_out), .clk(clock_1_out), .ld(main_4_read));  // open: clr
  Clock clock_1 (.out(clock_1_out));

  // Notes on the sheet:
  //   contents of rom_1 (hex, n*v repeats v):
  //   2c3 10002 20040 40 406 40 2c3 3040 2c3 1400a e0040 40 2c3 1000e 9400f e0040 16*0 1000 31*0 c0041
  //   12842 a01a0 a0130 a0120
endmodule
