// Logisim project Contol Unit.circ as structural Verilog: 1 circuit, main circuit main
module main (
  input  CLR_AR,
  input  DR_13,
  input  DR_11,
  input  in_4,
  input  DR_9,
  input  in_6,
  input  DR_7,
  input  in_8,
  input  DR_5,
  input  in_10,
  input  DR_3,
  input  in_12,
  input  DR_1,
  input  in_14,
  input  AC_15,
  input  in_16,
  input  AC_13,
  input  in_18,
  input  AC_11,
  input  in_20,
  input  AC_9,
  input  in_22,
  input  AC_7,
  input  in_24,
  input  AC_5,
  input  in_26,
  input  AC_3,
  input  in_28,
  input  AC_1,
  input  in_30,
  input  in_31,
  input  E,
  input  in_33,
  input  I,
  input  D7,
  input  D6,
  input  D5,
  input  D4,
  input  D3,
  input  D2,
  input  D1,
  input  D0,
  input  IR_10,
  input  IR_8,
  input  IR_9,
  input  IR_6,
  input  IR_7,
  input  IR_4,
  input  IR_5,
  input  in_50,
  input  IR_2,
  input  in_52,
  input  IR_0,
  input  T,
  input  T0,
  input  T1,
  input  T2,
  input  T3,
  input  T4,
  input  T5,
  input  T6,
  input  T7,
  input  T8,
  input  T9,
  input  T10,
  input  T12,
  input  T11,
  input  T14,
  input  T13,
  input  in_70,
  input  R,
  input  S,
  input  in_73,
  input  FGI,
  input  in_75,
  input  in_76,
  output LD_TR,
  output LD_AR,
  output out_79,
  output LD_IR,
  output x5,
  output LD_DR,
  output Read,
  output INR_AR,
  output INR_DR,
  output x3,
  output CLR_SC,
  output CLR_PC,
  output Write,
  output x6,
  output x2,
  output x4,
  output x7,
  output CLR_AC,
  output LD_AC,
  output J_E,
  output K_E,
  output INR_AC,
  output INR_PC,
  output LD_OUTR,
  output J_IEN,
  output x1,
  output K_FGI,
  output K_IEN,
  output LD_PC,
  output J_FGI,
  output K_FGO,
  output K_S,
  output J_FGO,
  output J_S,
  output J_R,
  output K_R,
  output INPR,
  output SHR,
  output AND,
  output COM,
  output SHL,
  output ADD,
  output DR
);

  wire and_1_out, and_2_out, and_3_out, and_4_out, and_5_out, and_6_out, and_7_out, and_8_out, and_9_out,
       and_10_out, and_11_out, and_12_out, and_14_out, and_15_out, and_16_out, and_17_out, and_18_out,
       and_19_out, and_20_out, and_21_out, and_22_out, and_23_out, and_24_out, and_25_out, and_26_out,
       and_27_out, and_28_out, and_29_out, and_30_out, and_31_out, and_32_out, and_35_out, and_36_out,
       and_37_out, and_38_out, and_41_out, and_42_out, and_43_out, and_44_out, and_45_out, and_46_out,
       and_47_out, and_48_out, and_49_out, and_50_out, and_51_out, and_52_out, and_53_out, and_54_out,
       and_55_out, and_56_out, and_57_out, and_58_out, and_59_out, and_60_out, and_61_out, and_62_out,
       and_63_out, and_64_out, and_65_out, and_66_out, and_67_out, and_68_out, and_69_out, and_70_out,
       and_74_out, and_75_out, and_76_out, and_77_out, and_78_out, and_79_out, and_80_out, and_81_out,
       and_86_out, and_87_out, and_88_out, and_89_out, and_90_out, and_93_out, and_105_out, and_106_out,
       not_1_out, not_2_out, not_3_out, not_4_out, not_5_out, not_6_out, not_7_out, not_8_out, not_9_out,
       not_10_out, not_11_out, not_12_out, not_13_out, or_1_out, or_2_out, or_3_out, or_4_out, or_5_out,
       or_6_out, or_8_out, or_10_out, or_11_out, or_12_out, or_13_out, or_14_out, or_15_out, or_16_out,
       or_17_out, or_18_out, or_19_out, or_20_out, or_21_out, or_22_out, or_23_out, or_24_out, or_25_out,
       or_26_out, or_27_out, or_28_out, or_29_out, or_30_out, or_31_out, or_32_out, or_33_out, or_34_out,
       or_35_out, or_36_out, or_37_out, or_38_out, or_39_out, or_40_out, or_41_out, or_42_out, or_43_out,
       or_44_out, or_45_out, or_46_out;

  not not_1 (not_1_out, I);
  not not_2 (not_2_out, D7);
  and and_1 (and_1_out, I, D7, T4);
  and and_2 (and_2_out, not_1_out, D7, T0);
  and and_3 (and_3_out, D7, I, T0);
  and and_4 (and_4_out, not_1_out, D7, T4);
  and and_5 (and_5_out, D0, T0);
  and and_6 (and_6_out, D1, T0);
  and and_7 (and_7_out, D2, T0);
  and and_8 (and_8_out, D4, T0);
  and and_9 (and_9_out, D5, T0);
  or or_1 (or_1_out, and_8_out, and_9_out);
  and and_10 (and_10_out, D6, T0);
  and and_11 (and_11_out, D3, T0);
  not not_3 (not_3_out, T2);
  not not_4 (not_4_out, T1);
  and and_12 (and_12_out, T5, I, D7);
  and and_13 (LD_PC, or_1_out, in_73);
  not not_5 (not_5_out, T3);
  and and_14 (and_14_out, I, not_2_out, T4);
  and and_15 (and_15_out, S, T0);
  and and_16 (and_16_out, IR_10, and_2_out);
  and and_17 (and_17_out, IR_8, and_2_out);
  and and_18 (and_18_out, IR_9, and_2_out);
  and and_19 (and_19_out, IR_6, and_2_out);
  and and_20 (and_20_out, IR_7, and_2_out);
  and and_21 (and_21_out, IR_4, and_2_out);
  and and_22 (and_22_out, IR_5, and_2_out);
  and and_23 (and_23_out, in_50, and_2_out);
  and and_24 (and_24_out, IR_2, and_2_out);
  and and_25 (and_25_out, in_52, and_2_out);
  and and_26 (and_26_out, IR_0, and_2_out);
  and and_27 (and_27_out, IR_10, and_3_out);
  and and_28 (and_28_out, IR_8, and_3_out);
  and and_29 (and_29_out, IR_9, and_3_out);
  and and_30 (and_30_out, IR_6, and_3_out);
  and and_31 (and_31_out, IR_7, and_3_out);
  and and_32 (and_32_out, IR_4, and_3_out);
  and and_33 (INPR, and_27_out, in_73);
  and and_34 (COM, and_18_out, in_73);
  and and_35 (and_35_out, D0, T0);
  or or_2 (or_2_out, and_35_out, and_36_out, and_37_out);
  and and_36 (and_36_out, D1, T0);
  and and_37 (and_37_out, D2, T0);
  and and_38 (and_38_out, D5, T7);
  and and_39 (SHR, in_73, and_20_out);
  and and_40 (SHL, in_73, and_21_out);
  not not_6 (not_6_out, S);
  and and_41 (and_41_out, not_4_out, not_3_out, not_5_out, FGI, or_3_out);
  or or_3 (or_3_out, in_75, in_76);
  or or_4 (or_4_out, and_31_out, and_32_out);
  and and_42 (and_42_out, not_6_out, T3);
  and and_43 (and_43_out, D0, T5);
  and and_44 (and_44_out, D0, T6);
  and and_45 (and_45_out, D1, T5);
  and and_46 (and_46_out, T6, T5);
  and and_47 (and_47_out, D2, T5);
  and and_48 (and_48_out, D2, T6);
  and and_49 (and_49_out, D3, T5);
  and and_50 (and_50_out, D4, T5);
  and and_51 (and_51_out, D5, T5);
  and and_52 (and_52_out, D5, T6);
  and and_53 (and_53_out, D6, T5);
  and and_54 (and_54_out, D6, T6);
  and and_55 (and_55_out, D6, T7);
  and and_56 (and_56_out, S, T1);
  and and_57 (and_57_out, S, T2);
  and and_58 (and_58_out, S, T3);
  and and_59 (and_59_out, IR_10, and_4_out);
  and and_60 (and_60_out, IR_8, and_4_out);
  and and_61 (and_61_out, IR_9, and_4_out);
  and and_62 (and_62_out, IR_6, and_4_out);
  and and_63 (and_63_out, IR_7, and_4_out);
  and and_64 (and_64_out, IR_4, and_4_out);
  and and_65 (and_65_out, IR_5, and_4_out);
  and and_66 (and_66_out, in_50, and_4_out);
  and and_67 (and_67_out, IR_2, and_4_out);
  and and_68 (and_68_out, in_52, and_4_out);
  and and_69 (and_69_out, IR_0, and_4_out);
  and and_70 (and_70_out, T, and_4_out);
  and and_71 (AND, in_73, and_5_out);
  and and_72 (ADD, in_73, and_6_out);
  and and_73 (DR, in_73, and_7_out);
  and and_74 (and_74_out, not_6_out, T1);
  and and_75 (and_75_out, not_6_out, T2);
  and and_76 (and_76_out, IR_10, and_1_out);
  and and_77 (and_77_out, IR_8, and_1_out);
  and and_78 (and_78_out, IR_9, and_1_out);
  and and_79 (and_79_out, IR_6, and_1_out);
  and and_80 (and_80_out, IR_7, and_12_out);
  and and_81 (and_81_out, IR_4, and_1_out);
  and and_82 (LD_AR, and_56_out, in_73);
  or or_5 (or_5_out, and_74_out, and_42_out, and_14_out);
  and and_83 (x5, and_42_out, in_73);
  or or_6 (or_6_out, and_43_out, and_45_out, and_47_out, and_53_out);
  // OR_Gate or_7 has open pins: in0=and_44_out, in1=and_46_out, in2=and_48_out, out=open
  and and_84 (INR_DR, and_54_out, in_73);
  or or_8 (or_8_out, and_56_out, and_52_out, and_74_out);
  and and_85 (x2, or_8_out, in_73);
  and and_86 (and_86_out, not_11_out, and_23_out);
  and and_87 (and_87_out, AC_13, and_24_out);
  and and_88 (and_88_out, not_12_out, and_25_out);
  and and_89 (and_89_out, in_75, and_29_out);
  and and_90 (and_90_out, in_76, and_30_out);
  not not_7 (not_7_out, and_27_out);
  not not_8 (not_8_out, and_28_out);
  and and_91 (out_79, in_73, or_5_out);
  and and_92 (LD_IR, in_73, and_75_out);
  and and_93 (and_93_out, not_9_out, and_10_out);
  and and_94 (LD_DR, in_73, or_6_out);
  // OR_Gate or_9 has open pins: in0=and_50_out, in1=and_52_out, out=open
  and and_95 (INR_AR, and_51_out, in_73);
  and and_96 (CLR_PC, in_73, and_57_out);
  or or_10 (or_10_out, and_18_out, and_20_out, and_21_out, and_27_out);
  or or_11 (or_11_out, and_86_out, and_87_out, and_88_out);
  and and_97 (LD_OUTR, in_73, and_28_out);
  or or_12 (or_12_out, and_89_out, and_90_out);
  and and_98 (K_FGI, in_73, and_27_out);
  and and_99 (J_FGI, not_7_out, in_73);
  and and_100 (K_FGO, in_73, and_28_out);
  and and_101 (J_FGO, not_8_out, in_73);
  or or_13 (or_13_out, and_75_out, and_58_out, and_93_out);
  and and_102 (CLR_AC, in_73, and_16_out);
  or or_14 (or_14_out, or_2_out, or_10_out);
  and and_103 (LD_AC, or_14_out, in_73);
  and and_104 (INR_AC, and_22_out, in_73);
  or or_15 (or_15_out, CLR_AR, DR_13, DR_11, in_4);
  not not_9 (not_9_out, or_17_out);
  and and_105 (and_105_out, and_26_out, not_13_out);
  and and_106 (and_106_out, and_105_out, in_73);
  not not_10 (not_10_out, and_70_out);
  or or_16 (or_16_out, DR_9, in_6, DR_7, in_8);
  or or_17 (or_17_out, or_15_out, or_16_out, or_19_out, or_23_out);
  or or_18 (or_18_out, or_13_out, or_11_out, and_106_out, or_12_out);
  or or_19 (or_19_out, DR_5, in_10, DR_3, in_12);
  or or_20 (or_20_out, and_48_out, and_10_out);
  or or_21 (or_21_out, and_11_out, and_28_out);
  or or_22 (or_22_out, or_18_out, and_15_out);
  buf and_107 (K_S, and_70_out);  // AND_Gate
  buf and_108 (J_S, not_10_out);  // AND_Gate
  and and_109 (J_R, in_73, and_41_out);
  and and_110 (K_R, in_73, and_15_out);
  or or_23 (or_23_out, DR_1, in_14, AC_15, in_16);
  not not_11 (not_11_out, AC_13);
  and and_111 (x3, or_20_out, in_73);
  and and_112 (x4, or_21_out, in_73);
  and and_113 (INR_PC, or_22_out, in_73);
  or or_24 (or_24_out, AC_13, in_18, AC_11, in_20);
  not not_12 (not_12_out, or_27_out);
  or or_25 (or_25_out, and_43_out, and_45_out, and_47_out, and_53_out);
  or or_26 (or_26_out, AC_9, in_22, AC_7, in_24);
  or or_27 (or_27_out, or_24_out, or_26_out, or_28_out, or_30_out);
  or or_28 (or_28_out, AC_5, in_26, AC_3, in_28);
  or or_29 (or_29_out, or_25_out, and_75_out, and_38_out, and_14_out);
  or or_30 (or_30_out, AC_1, in_30, in_31, E);
  not not_13 (not_13_out, in_33);
  and and_114 (x7, or_29_out, in_73);
  or or_31 (or_31_out, and_53_out, and_75_out, and_14_out, and_43_out, and_45_out, and_47_out);
  or or_32 (or_32_out, and_58_out, and_44_out, and_46_out);
  or or_33 (or_33_out, and_48_out, and_49_out, and_50_out);
  or or_34 (or_34_out, and_51_out, and_55_out, and_59_out);
  or or_35 (or_35_out, and_10_out, and_51_out, and_11_out, CLR_PC);
  or or_36 (or_36_out, and_60_out, and_61_out, and_62_out);
  or or_37 (or_37_out, and_63_out, and_64_out, and_65_out);
  or or_38 (or_38_out, and_66_out, and_67_out, and_68_out);
  or or_39 (or_39_out, and_69_out, and_76_out);
  or or_40 (or_40_out, and_77_out, and_78_out, and_79_out);
  or or_41 (or_41_out, and_80_out, and_81_out);
  and and_115 (Write, or_35_out, in_73);
  or or_42 (or_42_out, or_31_out, and_38_out);
  and and_116 (J_IEN, or_4_out, in_73);
  and and_117 (K_IEN, in_73, and_15_out);
  and and_118 (Read, or_42_out, in_73);
  or or_43 (or_43_out, or_32_out, or_33_out, or_34_out, or_36_out, or_37_out);
  or or_44 (or_44_out, and_19_out, and_17_out);
  or or_45 (or_45_out, or_38_out, or_39_out, or_40_out, or_41_out);
  and and_119 (J_E, and_19_out, in_73);
  and and_120 (K_E, or_44_out, in_73);
  or or_46 (or_46_out, or_43_out, or_45_out);
  and and_121 (CLR_SC, or_46_out, in_73);

  assign LD_TR = LD_AR;
  assign x1 = LD_PC;
  assign x6 = CLR_PC;

  // Notes on the sheet:
  //   D7.I.T3 (p)
  //   D7.I'.T(r')
  //   D7.I.T(p')
  //   D7.I'.T3 (r)
  //   IR[11]
  //   IR[1]
  //   IR[3]
  //   r'.B11
  //   r'.B10
  //   r'.B9
  //   r'.B8
  //   r'.B7
  //   r'.B6
  //   r'.B5
  //   r'.B4
  //   r'.B3
  //   r'.B2
  //   r'.B1
  //   p'.B11
  //   p'.B10
  //   p'.B9
  //   p'.B8
  //   p'.B7
  //   p'.B6
  //   D7'.I.T3
  //   D0.T
  //   D1.T
  //   D2.T
  //   T15
  //   T0'.T1'.T2'.IEN.(FGI+FGO)
  //   FGO
  //   IEN
  //   R'.T0
  //   R'.T1
  //   R'.T2
  //   D0.T4
  //   D0.T5
  //   D1.T4
  //   D1.T5
  //   D2.T4
  //   D2.T5
  //   D3.T4
  //   D4.T4
  //   D5.T4
  //   D5.T5
  //   D6.T4
  //   D6.T5
  //   D6.T6
  //   R.T0
  //   R.T1
  //   R.T2
  //   r.IR[11]
  //   r.IR[10]
  //   r.IR[9]
  //   r.IR[8]
  //   r.IR[7]
  //   r.IR[6]
  //   r.IR[5]
  //   r.IR[4]
  //   r.IR[3]
  //   r.IR[2]
  //   r.IR[1]
  //   r.IR[0]
  //   p.IR[11]
  //   p.IR[10]
  //   p.IR[9]
  //   p.IR[8]
  //   p.IR[7]
  //   p.IR[6]
  //   DR[14]
  //   DR[15]
  //   DR[12]
  //   DR[10]
  //   DR[6]
  //   DR[8]
  //   DR
  //   DR[2]
  //   DR[4]
  //   DR[0]
  //   AC[14]
  //   AC[15]
  //   AC[12]
  //   AC[10]
  //   AC[6]
  //   AC[8]
  //   AC
  //   AC[4]
  //   AC[2]
  //   AC[0]
endmodule
