// Logisim project Control Unit COMP2.circ as structural Verilog: 1 circuit, main circuit main
module main (
  input  [2:0] F1,
  input  [2:0] F2,
  input  [2:0] F3,
  output ADD,
  output SU8,
  output OR,
  output AND,
  output XOR,
  output COMP,
  output LD_AC,
  output SHL,
  output SHR,
  output DRTAC,
  output INCAC,
  output CLRAC,
  output SEL_MUX1,
  output LD_AR,
  output READ,
  output LD_PC,
  output INCPC,
  output SEL_S1,
  output LD_DR,
  output SEL_S0,
  output INCDR,
  output WRITE,
  output WRITE_2
);

  wire and_13_out, decoder_1_out1, decoder_1_out2, decoder_1_out3, decoder_1_out4, decoder_1_out5,
       decoder_1_out6, decoder_1_out7, decoder_2_out1, decoder_2_out2, decoder_2_out3, decoder_2_out4,
       decoder_2_out5, decoder_2_out6, decoder_2_out7, decoder_3_out1, decoder_3_out2, decoder_3_out3,
       decoder_3_out4, decoder_3_out5, decoder_3_out6, decoder_3_out7, or_1_out, or_2_out, or_3_out, or_4_out;

  Decoder #(.select(3), .enable("false")) decoder_1 (
    .out1(decoder_1_out1), .out2(decoder_1_out2), .out3(decoder_1_out3), .out4(decoder_1_out4),
    .out5(decoder_1_out5), .out6(decoder_1_out6), .out7(decoder_1_out7), .sel(F1));  // open: out0
  Decoder #(.select(3), .enable("false")) decoder_2 (
    .out1(decoder_2_out1), .out2(decoder_2_out2), .out3(decoder_2_out3), .out4(decoder_2_out4),
    .out5(decoder_2_out5), .out6(decoder_2_out6), .out7(decoder_2_out7), .sel(F2));  // open: out0
  Decoder #(.select(3), .enable("false")) decoder_3 (
    .out1(decoder_3_out1), .out2(decoder_3_out2), .out3(decoder_3_out3), .out4(decoder_3_out4),
    .out5(decoder_3_out5), .out6(decoder_3_out6), .out7(decoder_3_out7), .sel(F3));  // open: out0
  buf and_1 (ADD, decoder_1_out1);  // AND_Gate
  buf and_2 (SU8, decoder_2_out1);  // AND_Gate
  buf and_3 (OR, decoder_2_out2);  // AND_Gate
  buf and_4 (AND, decoder_2_out3);  // AND_Gate
  buf and_5 (XOR, decoder_3_out1);  // AND_Gate
  buf and_6 (COMP, decoder_3_out2);  // AND_Gate
  buf and_7 (SHL, decoder_3_out3);  // AND_Gate
  buf and_8 (SHR, decoder_3_out4);  // AND_Gate
  buf and_9 (DRTAC, decoder_1_out4);  // AND_Gate
  buf and_10 (INCAC, decoder_1_out3);  // AND_Gate
  buf and_11 (CLRAC, decoder_1_out2);  // AND_Gate
  buf and_12 (SEL_MUX1, decoder_1_out5);  // AND_Gate
  buf and_13 (and_13_out, decoder_1_out6);  // AND_Gate
  buf and_14 (LD_PC, decoder_3_out6);  // AND_Gate
  buf and_15 (INCPC, decoder_3_out5);  // AND_Gate
  buf and_16 (READ, decoder_2_out4);  // AND_Gate
  buf and_17 (SEL_S1, decoder_2_out5);  // AND_Gate
  buf and_18 (SEL_S0, decoder_2_out7);  // AND_Gate
  buf and_19 (INCDR, decoder_2_out6);  // AND_Gate
  buf and_20 (WRITE, decoder_1_out7);  // AND_Gate
  buf and_21 (WRITE_2, decoder_3_out7);  // AND_Gate
  or or_1 (or_1_out, ADD, SU8);
  or or_2 (or_2_out, OR, AND);
  or or_3 (or_3_out, XOR, COMP);
  or or_4 (or_4_out, SHL, SHR);
  or or_5 (LD_AR, SEL_MUX1, and_13_out);
  or or_6 (LD_DR, READ, SEL_S1, SEL_S0);
  or or_7 (LD_AC, or_1_out, or_2_out, or_3_out, or_4_out, DRTAC);

  // Notes on the sheet:
  //   DRTAR
  //   SEL(S1)
  //   SEL(S0)
  //   ADD
  //   SUB
  //   OR
  //   AND
  //   XOR
  //   COM
  //   SHL
  //   SHR
  //   DRTAC
  //   INCAC
  //   CLRAC
  //   SEL(MUX1)
  //   LD(AR)
  //   LD(PC)
  //   INCPC
  //   READ
  //   ACTDR
  //   PCTDR
  //   INCDR
  //   WRITE
endmodule
