// Logisim project 11 bit Register.circ as structural Verilog: 1 circuit, main circuit main
module main (
  input  [10:0] in_1,
  input  in_2,
  input  in_3,
  input  in_4,
  input  in_5,
  output [10:0] out_6
);

  wire decoder_1_out1, or_1_out;
  wire [10:0] bit_extender_1_out, counter_1_q, main_1_output;

  Selection_for_11_bit_Register_main main_1 (
    .Input(in_1), .INR_Value(out_6), .Output(main_1_output), .LD(in_2), .INR(in_3));
  or or_1 (or_1_out, in_3, in_2);
  Counter #(.width(11), .max('h7ff)) counter_1 (
    .load(or_1_out), .D(main_1_output), .count(1'b0), .Q(counter_1_q), .clk(in_4), .clr(in_5));  // open: carry
  Decoder #(.enable("false")) decoder_1 (.out1(decoder_1_out1), .sel(in_3));  // open: out0
  assign bit_extender_1_out = {{10{1'b0}}, decoder_1_out1};  // Bit_Extender bit_extender_1
  Adder #(.width(11)) adder_1 (.a(bit_extender_1_out), .b(counter_1_q), .out(out_6));  // open: cin, cout
endmodule
