// Logisim project 12 bit Register.circ as structural Verilog: 1 circuit, main circuit main
module main (
  input  [11:0] in_1,
  input  in_2,
  input  in_3,
  input  in_4,
  input  in_5,
  output [11:0] out_6
);

  wire decoder_1_out0, decoder_1_out1, or_1_out;
  wire [11:0] bit_extender_1_out, counter_1_q, main_1_output;

  or or_1 (or_1_out, in_3, in_2);
  Selection_For_12_bit_Register_main main_1 (
    .Output(main_1_output), .LD(in_3), .INR(in_2), .Input(in_1), .INR_Value(out_6));
  Counter #(.width(12), .max('hfff)) counter_1 (
    .load(or_1_out), .D(main_1_output), .count(1'b0), .Q(counter_1_q), .clk(in_4), .clr(in_5));  // open: carry
  Decoder #(.enable("false")) decoder_1 (.out0(decoder_1_out0), .out1(decoder_1_out1), .sel(in_2));
  assign bit_extender_1_out = {{11{1'b0}}, decoder_1_out1};  // Bit_Extender bit_extender_1
  Adder #(.width(12)) adder_1 (.a(bit_extender_1_out), .b(counter_1_q), .out(out_6));  // open: cin, cout
endmodule
