// Logisim project 7 bit Register.circ as structural Verilog: 1 circuit, main circuit main
module main (
  input  [6:0] in_1,
  input  in_2,
  input  in_3,
  input  in_4,
  input  in_5,
  output [6:0] out_6
);

  wire decoder_1_out1, or_1_out;
  wire [6:0] bit_extender_1_out, counter_1_q, main_1_output;

  Selection_for_7_bit_Register_main main_1 (
    .Input(in_1), .INR_Value(out_6), .Output(main_1_output), .LD(in_2), .INR(in_3));
  or or_1 (or_1_out, in_2, in_3);
  Counter #(.width(7), .max('h7f)) counter_1 (
    .load(or_1_out), .D(main_1_output), .count(1'b0), .Q(counter_1_q), .clk(in_4), .clr(in_5));  // open: carry
  Decoder #(.enable("false")) decoder_1 (.out1(decoder_1_out1), .sel(in_3));  // open: out0
  assign bit_extender_1_out = {{6{1'b0}}, decoder_1_out1};  // Bit_Extender bit_extender_1
  Adder #(.width(7)) adder_1 (.a(bit_extender_1_out), .b(counter_1_q), .out(out_6));  // open: cin, cout
endmodule
