// Logisim project OUTR Register.circ as structural Verilog: 1 circuit, main circuit main
module main (
  input  in_1,
  input  [7:0] in_2,
  input  in_3,
  output [7:0] out_4
);

  Counter counter_1 (.load(in_1), .D(in_2), .count(1'b0), .Q(out_4), .clk(in_3));  // open: carry, clr
endmodule
