// Logisim project Selection For 12 bit Register.circ as structural Verilog: 1 circuit, main circuit main
module main (
  input  LD,
  input  INR,
  input  [11:0] Input,
  input  [11:0] INR_Value,
  output [11:0] Output
);

  wire [11:0] and_1_out, and_2_out;
  wire [11:11] comparator_1_gt, comparator_1_lt;

  Comparator #(.width(1), .mode("unsigned")) comparator_1 (
    .a(LD), .b(INR), .gt(comparator_1_gt[11]), .lt(comparator_1_lt[11]));  // open: eq
  assign and_1_out = Input & {12{comparator_1_gt[11]}};  // AND_Gate and_1, 12 bits wide
  assign and_2_out = {12{comparator_1_lt[11]}} & INR_Value;  // AND_Gate and_2, 12 bits wide
  assign Output = and_1_out | and_2_out;  // OR_Gate or_1, 12 bits wide
endmodule
