// Logisim project Selection For 16 bit Register.circ as structural Verilog: 1 circuit, main circuit main
module main (
  input  LD,
  input  INR,
  input  [15:0] Input,
  input  [15:0] INR_Value,
  output [15:0] Output
);

  wire [15:0] and_1_out, and_2_out;
  wire [15:15] comparator_1_gt, comparator_1_lt;

  Comparator #(.width(1), .mode("unsigned")) comparator_1 (
    .a(LD), .b(INR), .gt(comparator_1_gt[15]), .lt(comparator_1_lt[15]));  // open: eq
  assign and_1_out = Input & {16{comparator_1_gt[15]}};  // AND_Gate and_1, 16 bits wide
  assign and_2_out = {16{comparator_1_lt[15]}} & INR_Value;  // AND_Gate and_2, 16 bits wide
  assign Output = and_1_out | and_2_out;  // OR_Gate or_1, 16 bits wide
endmodule
