// Logisim project Selection for 11 bit Register.circ as structural Verilog: 1 circuit, main circuit main
module main (
  input  LD,
  input  INR,
  input  [10:0] Input,
  input  [10:0] INR_Value,
  output [10:0] Output
);

  wire [10:0] and_1_out, and_2_out;
  wire [10:10] comparator_1_gt, comparator_1_lt;

  Comparator #(.width(1), .mode("unsigned")) comparator_1 (
    .a(LD), .b(INR), .gt(comparator_1_gt[10]), .lt(comparator_1_lt[10]));  // open: eq
  assign and_1_out = Input & {11{comparator_1_gt[10]}};  // AND_Gate and_1, 11 bits wide
  assign and_2_out = {11{comparator_1_lt[10]}} & INR_Value;  // AND_Gate and_2, 11 bits wide
  assign Output = and_1_out | and_2_out;  // OR_Gate or_1, 11 bits wide
endmodule
