// Logisim project Selection for 7 bit Register.circ as structural Verilog: 1 circuit, main circuit main
module main (
  input  LD,
  input  INR,
  input  [6:0] Input,
  input  [6:0] INR_Value,
  output [6:0] Output
);

  wire [6:0] and_1_out, and_2_out;
  wire [6:6] comparator_1_gt, comparator_1_lt;

  Comparator #(.width(1), .mode("unsigned")) comparator_1 (
    .a(LD), .b(INR), .gt(comparator_1_gt[6]), .lt(comparator_1_lt[6]));  // open: eq
  assign and_1_out = Input & {7{comparator_1_gt[6]}};  // AND_Gate and_1, 7 bits wide
  assign and_2_out = {7{comparator_1_lt[6]}} & INR_Value;  // AND_Gate and_2, 7 bits wide
  assign Output = and_1_out | and_2_out;  // OR_Gate or_1, 7 bits wide
endmodule
